# Fritzing sketch midicontroller (saved by Fritzing 0.9.2b)
breadboards: 1

parts:
  Teensy_3_1 = Teensy 3.1
  Bauteil1 = LilyPad Button Board
  Bauteil2 = LilyPad Button Board
  Bauteil3 = LilyPad Button Board
  Bauteil4 = LilyPad Button Board
  Bauteil5 = LilyPad Button Board
  Bauteil6 = LilyPad Button Board
  Bauteil7 = LilyPad Button Board
  Bauteil8 = LilyPad Button Board
  Bauteil9 = LilyPad Button Board
  Bauteil10 = LilyPad Button Board
  LED1 = LED - 5mm [color="Red (633nm)" package="5 mm [THT]"]
  LED2 = LED - 5mm [color="Red (633nm)" package="5 mm [THT]"]
  LED3 = LED - 5mm [color="Red (633nm)" package="5 mm [THT]"]
  LED4 = LED - 5mm [color="Red (633nm)" package="5 mm [THT]"]
  LED5 = LED - 5mm [color="Red (633nm)" package="5 mm [THT]"]
  LED6 = LED - 5mm [color="Red (633nm)" package="5 mm [THT]"]
  LED7 = LED - 5mm [color="Red (633nm)" package="5 mm [THT]"]
  LED8 = LED - 5mm [color="Red (633nm)" package="5 mm [THT]"]
  LED9 = LED - 5mm [color="Red (633nm)" package="5 mm [THT]"]
  LED10 = LED - 5mm [color="Red (633nm)" package="5 mm [THT]"]
  R1 = Resistor [tolerance=±5% resistance=220 package=THT]
  R2 = Resistor [tolerance=±5% resistance=220 package=THT]
  R3 = Resistor [tolerance=±5% resistance=220 package=THT]
  R4 = Resistor [tolerance=±5% resistance=220 package=THT]
  R5 = Resistor [tolerance=±5% resistance=220 package=THT]
  R6 = Resistor [tolerance=±5% resistance=220 package=THT]
  R7 = Resistor [tolerance=±5% resistance=220 package=THT]
  R8 = Resistor [tolerance=±5% resistance=220 package=THT]
  R9 = Resistor [tolerance=±5% resistance=220 package=THT]
  R10 = Resistor [tolerance=±5% resistance=220 package=THT]
  R11 = Resistor [tolerance=±5% resistance=220 package=THT]
  LED11 = LED - 5mm [color="Red (633nm)" package="5 mm [THT]"]

nets:
  N1: Teensy_3_1.GND, Bauteil7.S, Bauteil8.S, Bauteil9.S, Bauteil10.S, LED1.cathode, LED2.cathode, LED3.cathode, LED4.cathode, LED5.cathode, LED6.cathode, LED7.cathode, LED8.cathode, LED9.cathode, LED10.cathode, LED11.cathode
  N2: Teensy_3_1.D0, Bauteil1.-
  N3: Teensy_3_1.D1, Bauteil2.-
  N4: Teensy_3_1.D2, Bauteil3.-
  N5: Teensy_3_1.D3, Bauteil4.-
  N6: Teensy_3_1.D4, Bauteil5.-
  N7: Teensy_3_1.D5, Bauteil6.-
  N8: Teensy_3_1.D6, Bauteil7.-
  N9: Teensy_3_1.D7, Bauteil8.-
  N10: Teensy_3_1.D8, Bauteil9.-
  N11: Teensy_3_1.D9, Bauteil10.-
  N12: Teensy_3_1.D10, R1.Pin_1
  N13: Teensy_3_1.D11, R2.Pin_1
  N14: Teensy_3_1.D12, R3.Pin_1
  N15: Teensy_3_1.A0/D14, R4.Pin_1
  N16: Teensy_3_1.A1/D15, R5.Pin_1
  N17: Teensy_3_1.A2/D16, R6.Pin_1
  N18: Teensy_3_1.A3/D17, R7.Pin_1
  N19: Teensy_3_1.A6/D20, R8.Pin_1
  N20: Teensy_3_1.A7/D21, R9.Pin_1
  N21: Teensy_3_1.A8/D22, R10.Pin_1
  N22: Teensy_3_1.A9/D23, R11.Pin_1
  N23: Teensy_3_1.Vin, Bauteil1.S, Bauteil2.S, Bauteil3.S, Bauteil4.S, Bauteil5.S, Bauteil6.S
  N24: LED1.anode, R1.Pin_0
  N25: LED2.anode, R2.Pin_0
  N26: LED3.anode, R3.Pin_0
  N27: LED4.anode, R4.Pin_0
  N28: LED5.anode, R5.Pin_0
  N29: LED6.anode, R6.Pin_0
  N30: LED7.anode, R9.Pin_0
  N31: LED8.anode, R10.Pin_0
  N32: LED9.anode, R7.Pin_0
  N33: LED10.anode, R8.Pin_0
  N34: R11.Pin_0, LED11.anode
